# Fritzing sketch truck (saved by Fritzing 0.8.3b)
breadboards: 1

parts:
  Part1 = Arduino Uno (Rev3)
  Q1 = NPN-Transistor [package="TO92 [THT]"]
  Q2 = NPN-Transistor [package="TO92 [THT]"]
  Q3 = NPN-Transistor [package="TO92 [THT]"]
  R2 = Resistor [tolerance=±5% resistance=100k package=THT]
  R3 = Resistor [tolerance=±5% resistance=100k package=THT]
  R4 = Resistor [tolerance=±5% resistance=100k package=THT]
  LED1 = LED - 5mm [color="Red (633nm)" package="5 mm [THT]"]
  LED2 = LED - 5mm [color="Red (633nm)" package="5 mm [THT]"]
  LED3 = LED - 5mm [color="Red (633nm)" package="5 mm [THT]"]
  VCC1 = 4 x AAA Battery Mount
  S1 = Pushbutton [package="[THT]"]
  S2 = Pushbutton [package="[THT]"]
  S3 = Pushbutton [package="[THT]"]
  R5 = Resistor [tolerance=±5% resistance=100k package=THT]
  R6 = Resistor [tolerance=±5% resistance=100k package=THT]
  R7 = Resistor [tolerance=±5% resistance=100k package=THT]

nets (from the schematic view):
  N1: Part1.ICSP_MISO, Part1.D12/MISO, Q2.B, R3.Pin_0
  N2: Part1.ICSP_SCK, Part1.D13/SCK, Q3.B, R2.Pin_0
  N3: Part1.ICSP_MOSI, Part1.D11_PWM/MOSI, Q1.B, R4.Pin_0
  N4: Part1.GND, R2.Pin_1, R3.Pin_1, R4.Pin_1, R5.Pin_0, R6.Pin_0, R7.Pin_0
  N5: Part1.D5_PWM, S1.Pin_3, S1.Pin_4, R7.Pin_1
  N6: Part1.D6_PWM, S2.Pin_3, S2.Pin_4, R6.Pin_1
  N7: Part1.D7, S3.Pin_3, S3.Pin_4, R5.Pin_1
  N8: Part1.3V3, S1.Pin_1, S1.Pin_2, S2.Pin_1, S2.Pin_2, S3.Pin_1, S3.Pin_2
  N9: Q1.E, LED3.anode
  N10: Q1.C, Q2.C, Q3.C, VCC1.+
  N11: Q2.E, LED1.anode
  N12: Q3.E, LED2.anode
  N13: LED1.cathode, LED2.cathode, LED3.cathode, VCC1.-
